// Digital circuit Locker.dig as structural Verilog
module Locker (
  input  RESET,
  input  CLOCK,
  output [6:0] out_3,
  output [15:0] out_4
);

  wire _0_out, _1_out, _2_out, _3_out, _4_out, _5_out, _6_out, _7_out, _8_out, _9_out, and_1_out, and_2_out,
       ID_2_out, PASS_2_out, u_encoder_da, u_mode_selector_ido, u_mode_selector_pwdo, u_shifter_pwd_led1,
       u_shifter_pwd_led2, u_shifter_pwd_led3, u_shifter_pwd_led4, u_shifter_pwd_match, u_timer_dis,
       u_timer_reset, u_timer_timeout;
  wire [3:0] u_encoder_data, u_shifter_id0, u_shifter_id1;

  Button _1 (.out(_1_out));
  Button _4 (.out(_4_out));
  Button _7 (.out(_7_out));
  Button _2 (.out(_2_out));
  Button _5 (.out(_5_out));
  Button _8 (.out(_8_out));
  Button _0 (.out(_0_out));
  Button _3 (.out(_3_out));
  Button _6 (.out(_6_out));
  Button _9 (.out(_9_out));
  LED ID (.in(u_mode_selector_ido));
  LED PASS (.in(u_mode_selector_pwdo));
  Button ID_2 (.out(ID_2_out));
  Button PASS_2 (.out(PASS_2_out));
  mode_selector #(.applicationType("IVERILOG")) u_mode_selector (
    .ID(ID_2_out), .PWD(PASS_2_out), .DIS(u_timer_dis), .RESET(u_timer_reset), .CLK(CLOCK), .RST(RESET),
    .MATCH(u_shifter_pwd_match), .IDO(u_mode_selector_ido), .PWDO(u_mode_selector_pwdo));
  encoder #(.applicationType("IVERILOG")) u_encoder (
    .P0(_0_out), .P1(_1_out), .P2(_2_out), .P3(_3_out), .P4(_4_out), .P5(_5_out), .P6(_6_out), .P7(_7_out),
    .P8(_8_out), .P9(_9_out), .CLK(CLOCK), .RST(RESET), .DATA(u_encoder_data), .DA(u_encoder_da));
  ROM #(.AddrBits(7), .isProgramMemory("true"), .Bits(16)) Password (.A(out_3), .sel(1'b1), .D(out_4));
  timer #(.applicationType("IVERILOG")) u_timer (
    .START(u_shifter_pwd_led4), .CLK(CLOCK), .RST(RESET), .RESET(u_timer_reset), .DIS(u_timer_dis),
    .TIMEOUT(u_timer_timeout));
  shifter #(.applicationType("IVERILOG")) u_shifter (
    .IN(u_encoder_data), .EN(u_mode_selector_ido), .DA(u_encoder_da), .CLK(CLOCK), .RST(RESET),
    .ID1(u_shifter_id1), .ID0(u_shifter_id0), .HEX(out_3));
  shifter_pwd #(.applicationType("IVERILOG")) u_shifter_pwd (
    .DATA_in(u_encoder_data), .PWD_in(out_4), .EN(u_mode_selector_pwdo), .DA(u_encoder_da), .CLK(CLOCK),
    .RST(RESET), .TIMEOUT(u_timer_timeout), .MATCH(u_shifter_pwd_match), .LED1(u_shifter_pwd_led1),
    .LED2(u_shifter_pwd_led2), .LED3(u_shifter_pwd_led3), .LED4(u_shifter_pwd_led4));
  Seven_Seg_Hex seven_seg_hex_1 (.d(u_shifter_id1), .dp(1'b0));
  Seven_Seg_Hex seven_seg_hex_2 (.d(u_shifter_id0), .dp(1'b0));
  LED led_1 (.in(u_shifter_pwd_led1));
  LED led_2 (.in(u_shifter_pwd_led2));
  and and_1 (and_1_out, u_shifter_pwd_match, u_shifter_pwd_led4);
  and and_2 (and_2_out, ~u_shifter_pwd_match, u_shifter_pwd_led4);  // And
  LED led_3 (.in(u_shifter_pwd_led3));
  LED led_4 (.in(u_shifter_pwd_led4));
  LED GRANTED (.in(and_1_out));
  LED DENIED (.in(and_2_out));

  // Notes on the sheet:
  //   CLOCK: Hz: 100
  //   contents of Password (hex, n*v repeats v):
  //   1234,5678,2341,505,2717,0,1504,28*ffff,1919,17*ffff,5555,17*ffff
  //   ,4201,27*ffff
  //   Arman Gökalp
endmodule

/* Code of mode_selector:
module mode_selector(
    	input wire ID, PWD, DIS, RESET, CLK, RST, MATCH,
    	output reg IDO, PWDO
);
    	always @(posedge CLK or posedge RST) begin
        	if (!RST) begin
            		IDO <= 1;
            		PWDO <= 0;
        	end else begin
            		if (ID || MATCH) begin
                		IDO <= 1;
                		PWDO <= 0;
            		end
            		if (PWD && !MATCH) begin
                		PWDO <= 1;
                		IDO <= 0;
            		end
    		end
	end
endmodule
*/

/* Code of encoder:
module encoder(
	input P0, P1, P2, P3, P4, P5, P6, P7, P8, P9,
	input CLK, RST,
	output reg [3:0] DATA,
	output reg DA);
	
	reg pressed;
	wire button;

	assign button = P0|P1|P2|P3|P4|P5|P6|P7|P8|P9;

	always @(posedge CLK, negedge RST) 
		if(!RST)
		begin
			pressed <= 0;
			DATA <= 4'b0000;
		end
		else
		begin
			if(button)
			begin
				if(~pressed)
				begin
					pressed <= 1'b1;
					DA <= 1'b1;
				end
				else
					DA <= 1'b0;
				if      (P0) DATA <= 4'b0000;
				else if (P1) DATA <= 4'b0001;
				else if (P2) DATA <= 4'b0010;
				else if (P3) DATA <= 4'b0011;
				else if (P4) DATA <= 4'b0100;
				else if (P5) DATA <= 4'b0101;
				else if (P6) DATA <= 4'b0110;
				else if (P7) DATA <= 4'b0111;
				else if (P8) DATA <= 4'b1000;
				else         DATA <= 4'b1001;
			end
			else
			begin
				pressed <= 1'b0;
				DA <= 1'b0;
			end				
		end			
endmodule
*/

/* Code of timer:
module timer(
	input wire START, CLK, RST,
	output reg RESET, DIS,
	output reg TIMEOUT
);
	reg [7:0] counter;
    
	always @(posedge CLK or posedge RST) begin
		if (!RST) begin
			counter <= 0;
			RESET <= 0;
			DIS <= 0;
			TIMEOUT <= 0;
		end else if (START && counter < 300) begin
			counter <= counter + 1;
			if (counter >= 150) begin
				RESET <= 1;
				DIS <= 1;
				TIMEOUT <= 1;
				counter <= 0;
			end
		end else begin
			RESET <= 0;
			DIS <= 0;
			TIMEOUT <= 0;
		end
	end
endmodule
*/

/* Code of shifter:
module shifter(
	input wire [3:0] IN,
	input wire EN,
    	input wire DA,
    	input wire CLK,
    	input wire RST,
    	output reg [3:0] ID1, ID0,
    	output reg [6:0] HEX
);

    	always @(posedge CLK or posedge RST) begin
        	if (!RST) begin
            		ID1 <= 4'b0000;
            		ID0 <= 4'b0000;
        	end else if (EN && DA) begin
            		ID1 <= ID0;
            		ID0 <= IN;
        	end
    	end

    	always @* begin
        	case(IN)
            		4'b0000: HEX = ID1*10 + ID0;
            		4'b0001: HEX = ID1*10 + ID0;
            		4'b0010: HEX = ID1*10 + ID0;
            		4'b0011: HEX = ID1*10 + ID0;
            		4'b0100: HEX = ID1*10 + ID0;
            		4'b0101: HEX = ID1*10 + ID0;
            		4'b0110: HEX = ID1*10 + ID0;
            		4'b0111: HEX = ID1*10 + ID0;
            		4'b1000: HEX = ID1*10 + ID0;
            		4'b1001: HEX = ID1*10 + ID0;
            		default: HEX = ID1*10 + ID0;
		endcase
	end
endmodule
*/

/* Code of shifter_pwd:
module shifter_pwd(
	input wire [3:0] DATA_in, 
	input wire [15:0] PWD_in, 
	input wire EN, DA, CLK, RST, TIMEOUT,
	output reg MATCH, LED1, LED2, LED3, LED4
);
	reg [15:0] password;
	reg [3:0] count;

	always @(posedge CLK or posedge RST) begin
		if (!RST) begin
			password <= 0;
			count <= 0;
			MATCH <= 0;
		end else if (EN && DA) begin
			password <= password << 4;
			password[3:0] <= DATA_in;
			count <= count + 1;
		end
		if (count == 4) begin
			if (password == PWD_in) MATCH <= 1;
		end
	end

	always @(posedge TIMEOUT) begin
		password <= 0;
		count <= 0;
		MATCH <= 0;
	end

	always @* begin
		LED1 = (count >= 1) ? 1 : 0;
		LED2 = (count >= 2) ? 1 : 0;
		LED3 = (count >= 3) ? 1 : 0;
		LED4 = (count >= 4) ? 1 : 0;

		if (password != PWD_in) begin 
			MATCH <= 0; 
		end
	end
endmodule
*/
